// Logisim project accumulator_v2.circ as structural Verilog: 1 circuit, main circuit main
module main (
  input  [3:0] in_1,
  input  [3:0] in_2,
  input  [3:0] in_3,
  input  [1:0] in_4,
  input  ACC_LOAD,
  output [3:0] \output 
);

  wire CLK_out, multiplexer_1_out, multiplexer_2_out, multiplexer_4_out, multiplexer_5_out;
  wire [3:0] multiplexer_3_out;

  Clock CLK (.out(CLK_out));
  D_Flip_Flop d_ff_1 (.D(multiplexer_1_out), .clk(CLK_out), .Q(\output [3]));  // open: Qn, preset, reset
  Multiplexer multiplexer_1 (.in0(\output [3]), .in1(multiplexer_3_out[3]), .out(multiplexer_1_out), .sel(ACC_LOAD));
  Multiplexer multiplexer_2 (.in0(\output [2]), .in1(multiplexer_3_out[2]), .out(multiplexer_2_out), .sel(ACC_LOAD));
  Multiplexer #(.select(2), .width(4)) multiplexer_3 (
    .in0(in_1), .in1(in_2), .in2(in_3), .out(multiplexer_3_out), .sel(in_4));  // open: in3
  D_Flip_Flop d_ff_2 (.D(multiplexer_2_out), .clk(CLK_out), .Q(\output [2]));  // open: Qn, preset, reset
  D_Flip_Flop d_ff_3 (.D(multiplexer_4_out), .clk(CLK_out), .Q(\output [1]));  // open: Qn, preset, reset
  Multiplexer multiplexer_4 (.in0(\output [1]), .in1(multiplexer_3_out[1]), .out(multiplexer_4_out), .sel(ACC_LOAD));
  D_Flip_Flop d_ff_4 (.D(multiplexer_5_out), .clk(CLK_out), .Q(\output [0]));  // open: Qn, preset, reset
  Multiplexer multiplexer_5 (.in0(\output [0]), .in1(multiplexer_3_out[0]), .out(multiplexer_5_out), .sel(ACC_LOAD));

  // Notes on the sheet:
  //   alu_input
  //   ram_in
  //   imm
endmodule
