// Logisim project 4BitALU_V2.circ as structural Verilog: 1 circuit, main circuit main
module main (
  input  [3:0] ACC_INPUT,
  input  [3:0] RAM_INPUT,
  input  [2:0] ALU_CTRL,
  output [3:0] ALU_OUT,
  output out_5
);

  wire and_1_out, and_2_out, and_3_out, and_4_out, and_5_out, and_6_out, and_7_out, and_8_out, and_9_out,
       and_10_out, and_11_out, and_12_out, and_13_out, and_14_out, and_15_out, and_16_out, and_17_out,
       and_18_out, and_20_out, and_21_out, and_22_out, and_23_out, and_24_out, and_25_out, and_26_out,
       and_27_out, and_28_out, and_29_out, and_30_out, and_31_out, and_32_out, and_33_out, and_34_out,
       and_35_out, and_36_out, and_37_out, decoder_1_out0, decoder_1_out1, decoder_1_out2, decoder_1_out3,
       not_1_out, not_2_out, not_3_out, not_4_out, not_5_out, not_6_out, not_7_out, not_8_out, or_1_out,
       or_2_out, or_3_out, or_4_out, or_5_out, or_6_out, or_7_out, or_8_out, or_9_out, or_10_out, or_13_out,
       or_14_out, or_18_out, or_19_out, or_20_out, or_21_out, xor_1_out, xor_2_out, xor_3_out, xor_4_out,
       xor_5_out, xor_6_out, xor_11_out, xor_12_out, xor_13_out, xor_14_out, xor_15_out, xor_16_out;
  wire [3:0] multiplexer_1_out, or_11_out, xor_7_out;

  xor xor_1 (xor_1_out, multiplexer_1_out[0], ALU_CTRL[0]);
  xor xor_2 (xor_2_out, ACC_INPUT[0], xor_1_out);
  and and_1 (and_1_out, xor_1_out, ACC_INPUT[0]);
  xor xor_3 (xor_3_out, ACC_INPUT[1], xor_6_out);
  and and_2 (and_2_out, xor_6_out, ACC_INPUT[1]);
  xor xor_4 (xor_4_out, ACC_INPUT[2], xor_11_out);
  and and_3 (and_3_out, xor_11_out, ACC_INPUT[2]);
  xor xor_5 (xor_5_out, ACC_INPUT[3], xor_12_out);
  and and_4 (and_4_out, xor_12_out, ACC_INPUT[3]);
  xor xor_6 (xor_6_out, multiplexer_1_out[1], ALU_CTRL[0]);
  xor xor_7 (xor_7_out[0], xor_2_out, ALU_CTRL[0]);
  and and_5 (and_5_out, xor_2_out, ALU_CTRL[0]);
  xor xor_8 (xor_7_out[1], xor_3_out, or_1_out);
  and and_6 (and_6_out, xor_3_out, or_1_out);
  xor xor_9 (xor_7_out[2], xor_4_out, or_2_out);
  and and_7 (and_7_out, xor_4_out, or_2_out);
  xor xor_10 (xor_7_out[3], xor_5_out, or_3_out);
  and and_8 (and_8_out, xor_5_out, or_3_out);
  xor xor_11 (xor_11_out, multiplexer_1_out[2], ALU_CTRL[0]);
  or or_1 (or_1_out, and_1_out, and_5_out);
  or or_2 (or_2_out, and_2_out, and_6_out);
  or or_3 (or_3_out, and_3_out, and_7_out);
  or or_4 (or_4_out, and_4_out, and_8_out);
  xor xor_12 (xor_12_out, multiplexer_1_out[3], ALU_CTRL[0]);
  not not_1 (not_1_out, ACC_INPUT[0]);
  not not_2 (not_2_out, ACC_INPUT[1]);
  and and_9 (and_9_out, ACC_INPUT[0], multiplexer_1_out[0]);
  or or_5 (or_5_out, ACC_INPUT[0], multiplexer_1_out[0]);
  xor xor_13 (xor_13_out, ACC_INPUT[0], multiplexer_1_out[0]);
  and and_10 (and_10_out, ACC_INPUT[1], multiplexer_1_out[1]);
  or or_6 (or_6_out, ACC_INPUT[1], multiplexer_1_out[1]);
  xor xor_14 (xor_14_out, ACC_INPUT[1], multiplexer_1_out[1]);
  and and_11 (and_11_out, and_9_out, decoder_1_out0);
  and and_12 (and_12_out, or_5_out, decoder_1_out1);
  and and_13 (and_13_out, decoder_1_out2, xor_13_out);
  and and_14 (and_14_out, decoder_1_out3, not_1_out);
  and and_15 (and_15_out, and_10_out, decoder_1_out0);
  and and_16 (and_16_out, or_6_out, decoder_1_out1);
  and and_17 (and_17_out, decoder_1_out2, xor_14_out);
  and and_18 (and_18_out, decoder_1_out3, not_2_out);
  Multiplexer #(.width(4)) multiplexer_1 (.in0(RAM_INPUT), .in1(4'b0001), .out(multiplexer_1_out), .sel(ALU_CTRL[1]));
  or or_7 (or_7_out, and_11_out, and_12_out);
  or or_8 (or_8_out, and_13_out, and_14_out);
  or or_9 (or_9_out, and_15_out, and_16_out);
  or or_10 (or_10_out, and_17_out, and_18_out);
  and and_19 (out_5, ALU_CTRL[2], or_4_out);
  Decoder #(.enable("false"), .select(2)) decoder_1 (
    .out0(decoder_1_out0), .out1(decoder_1_out1), .out2(decoder_1_out2), .out3(decoder_1_out3),
    .sel(ALU_CTRL[1:0]));
  or or_11 (or_11_out[0], or_7_out, or_8_out);
  or or_12 (or_11_out[1], or_9_out, or_10_out);
  and and_20 (and_20_out, xor_7_out[3], ALU_CTRL[2]);
  and and_21 (and_21_out, ACC_INPUT[2], multiplexer_1_out[2]);
  or or_13 (or_13_out, ACC_INPUT[2], multiplexer_1_out[2]);
  xor xor_15 (xor_15_out, ACC_INPUT[2], multiplexer_1_out[2]);
  not not_3 (not_3_out, ACC_INPUT[2]);
  and and_22 (and_22_out, ACC_INPUT[3], multiplexer_1_out[3]);
  or or_14 (or_14_out, ACC_INPUT[3], multiplexer_1_out[3]);
  xor xor_16 (xor_16_out, ACC_INPUT[3], multiplexer_1_out[3]);
  not not_4 (not_4_out, ACC_INPUT[3]);
  or or_15 (ALU_OUT[3], and_20_out, and_23_out);
  and and_23 (and_23_out, not_5_out, or_11_out[3]);
  and and_24 (and_24_out, xor_7_out[2], ALU_CTRL[2]);
  not not_5 (not_5_out, ALU_CTRL[2]);
  or or_16 (ALU_OUT[2], and_24_out, and_25_out);
  and and_25 (and_25_out, not_6_out, or_11_out[2]);
  and and_26 (and_26_out, xor_7_out[1], ALU_CTRL[2]);
  not not_6 (not_6_out, ALU_CTRL[2]);
  and and_27 (and_27_out, and_21_out, decoder_1_out0);
  and and_28 (and_28_out, or_13_out, decoder_1_out1);
  and and_29 (and_29_out, decoder_1_out2, xor_15_out);
  and and_30 (and_30_out, decoder_1_out3, not_3_out);
  and and_31 (and_31_out, and_22_out, decoder_1_out0);
  and and_32 (and_32_out, or_14_out, decoder_1_out1);
  and and_33 (and_33_out, decoder_1_out2, xor_16_out);
  and and_34 (and_34_out, decoder_1_out3, not_4_out);
  or or_17 (ALU_OUT[1], and_26_out, and_35_out);
  and and_35 (and_35_out, not_7_out, or_11_out[1]);
  and and_36 (and_36_out, xor_7_out[0], ALU_CTRL[2]);
  not not_7 (not_7_out, ALU_CTRL[2]);
  or or_18 (or_18_out, and_27_out, and_28_out);
  or or_19 (or_19_out, and_29_out, and_30_out);
  or or_20 (or_20_out, and_31_out, and_32_out);
  or or_21 (or_21_out, and_33_out, and_34_out);
  or or_22 (ALU_OUT[0], and_36_out, and_37_out);
  and and_37 (and_37_out, not_8_out, or_11_out[0]);
  not not_8 (not_8_out, ALU_CTRL[2]);
  or or_23 (or_11_out[2], or_18_out, or_19_out);
  or or_24 (or_11_out[3], or_20_out, or_21_out);

  // Notes on the sheet:
  //   constant
  //   CARRY
  //   000 → AND
  //   001 → OR
  //   010 → XOR
  //   011 → NOT
  //   100 → ADD
  //   101 → SUB
  //   NOT OPERATION FOR A INPUT ONLY
endmodule
