// Logisim project FLAG_REGISTERS.circ as structural Verilog: 1 circuit, main circuit main
module main (
  input  in_1,
  input  in_2,
  input  in_3,
  input  in_4,
  input  in_5,
  input  FLAG_EN,
  output out_7,
  output out_8
);

  wire CLK_out, multiplexer_1_out, multiplexer_2_out, not_1_out, or_1_out, or_2_out, or_3_out;

  Clock CLK (.out(CLK_out));
  D_Flip_Flop d_ff_1 (.D(multiplexer_1_out), .clk(CLK_out), .Q(out_7));  // open: Qn, preset, reset
  Multiplexer multiplexer_1 (.in0(out_7), .in1(in_1), .out(multiplexer_1_out), .sel(FLAG_EN));
  or or_1 (or_1_out, in_2, in_3);
  or or_2 (or_2_out, in_4, in_5);
  or or_3 (or_3_out, or_1_out, or_2_out);
  not not_1 (not_1_out, or_3_out);
  D_Flip_Flop d_ff_2 (.D(multiplexer_2_out), .clk(CLK_out), .Q(out_8));  // open: Qn, preset, reset
  Multiplexer multiplexer_2 (.in0(out_8), .in1(not_1_out), .out(multiplexer_2_out), .sel(FLAG_EN));

  // Notes on the sheet:
  //   CARRY
  //   CARRY FLAG
  //   ALU RESULT
  //   CARRY_FLAG_OP
  //   ZERO FLAG
  //   ZERO_FLAG_OP
endmodule
