// Logisim project FLAG_REGISTERS_V2.circ as structural Verilog: 1 circuit, main circuit main
module main (
  input  [3:0] ALU_RESULT,
  input  in_2,
  input  in_3,
  input  FLAG_EN,
  output CARRY_FLAG,
  output ZERO_FLAG
);

  wire CLK_out, multiplexer_1_out, multiplexer_2_out, multiplexer_3_out, not_1_out, or_1_out, or_2_out,
       or_3_out;

  Multiplexer multiplexer_1 (.in0(1'b0), .in1(in_2), .out(multiplexer_1_out), .sel(in_3));
  Clock CLK (.out(CLK_out));
  D_Flip_Flop d_ff_1 (.D(multiplexer_2_out), .clk(CLK_out), .Q(CARRY_FLAG));  // open: Qn, preset, reset
  Multiplexer multiplexer_2 (.in0(CARRY_FLAG), .in1(multiplexer_1_out), .out(multiplexer_2_out), .sel(FLAG_EN));
  or or_1 (or_1_out, ALU_RESULT[3], ALU_RESULT[2]);
  or or_2 (or_2_out, ALU_RESULT[1], ALU_RESULT[0]);
  or or_3 (or_3_out, or_1_out, or_2_out);
  not not_1 (not_1_out, or_3_out);
  D_Flip_Flop d_ff_2 (.D(multiplexer_3_out), .clk(CLK_out), .Q(ZERO_FLAG));  // open: Qn, preset, reset
  Multiplexer multiplexer_3 (.in0(ZERO_FLAG), .in1(not_1_out), .out(multiplexer_3_out), .sel(FLAG_EN));

  // Notes on the sheet:
  //   CARRY
  //   a or l
  //   CARRY_FLAG_OP
  //   ZERO_FLAG_OP
endmodule
