// Logisim project Instruction_Register.circ as structural Verilog: 1 circuit, main circuit main
module main (
  input  in_1,
  input  in_2,
  input  in_3,
  input  in_4,
  input  in_5,
  input  in_6,
  input  in_7,
  input  in_8,
  input  LOAD,
  output out_10,
  output out_11,
  output out_12,
  output out_13,
  output out_14,
  output out_15,
  output out_16,
  output out_17
);

  wire CLK_out, multiplexer_1_out, multiplexer_2_out, multiplexer_3_out, multiplexer_4_out,
       multiplexer_5_out, multiplexer_6_out, multiplexer_7_out, multiplexer_8_out;

  D_Flip_Flop d_ff_1 (.D(multiplexer_1_out), .clk(CLK_out), .Q(out_10));  // open: Qn, preset, reset
  Multiplexer multiplexer_1 (.in0(out_10), .in1(in_1), .out(multiplexer_1_out), .sel(LOAD));
  Clock CLK (.out(CLK_out));
  D_Flip_Flop d_ff_2 (.D(multiplexer_2_out), .clk(CLK_out), .Q(out_14));  // open: Qn, preset, reset
  Multiplexer multiplexer_2 (.in0(out_14), .in1(in_5), .out(multiplexer_2_out), .sel(LOAD));
  D_Flip_Flop d_ff_3 (.D(multiplexer_3_out), .clk(CLK_out), .Q(out_11));  // open: Qn, preset, reset
  Multiplexer multiplexer_3 (.in0(out_11), .in1(in_2), .out(multiplexer_3_out), .sel(LOAD));
  D_Flip_Flop d_ff_4 (.D(multiplexer_4_out), .clk(CLK_out), .Q(out_15));  // open: Qn, preset, reset
  Multiplexer multiplexer_4 (.in0(out_15), .in1(in_6), .out(multiplexer_4_out), .sel(LOAD));
  D_Flip_Flop d_ff_5 (.D(multiplexer_5_out), .clk(CLK_out), .Q(out_12));  // open: Qn, preset, reset
  Multiplexer multiplexer_5 (.in0(out_12), .in1(in_3), .out(multiplexer_5_out), .sel(LOAD));
  D_Flip_Flop d_ff_6 (.D(multiplexer_6_out), .clk(CLK_out), .Q(out_16));  // open: Qn, preset, reset
  Multiplexer multiplexer_6 (.in0(out_16), .in1(in_7), .out(multiplexer_6_out), .sel(LOAD));
  D_Flip_Flop d_ff_7 (.D(multiplexer_7_out), .clk(CLK_out), .Q(out_13));  // open: Qn, preset, reset
  Multiplexer multiplexer_7 (.in0(out_13), .in1(in_4), .out(multiplexer_7_out), .sel(LOAD));
  D_Flip_Flop d_ff_8 (.D(multiplexer_8_out), .clk(CLK_out), .Q(out_17));  // open: Qn, preset, reset
  Multiplexer multiplexer_8 (.in0(out_17), .in1(in_8), .out(multiplexer_8_out), .sel(LOAD));

  // Notes on the sheet:
  //   8 BIT INSTRUCTION
  //   4 BIT OPCODE
  //   4 BIT OPERAND
endmodule
