// Logisim project 16x8_RAM.circ as structural Verilog: 1 circuit, main circuit main
module main (
  input  in_1,
  input  in_2,
  input  in_3,
  input  in_4,
  input  in_5,
  input  in_6,
  input  in_7,
  input  in_8,
  input  in_9,
  input  in_10,
  input  in_11,
  input  in_12,
  input  READ_EN,
  input  WRITE_EN,
  input  in_15,
  input  in_16,
  input  in_17,
  input  in_18,
  output out_19,
  output out_20,
  output out_21,
  output out_22,
  output out_23,
  output out_24,
  output out_25,
  output out_26
);

  wire CLK_out, decoder_1_out0, decoder_1_out1, decoder_1_out2, decoder_1_out3, decoder_1_out4,
       decoder_1_out5, decoder_1_out6, decoder_1_out7, decoder_1_out8, decoder_1_out9, decoder_1_out10,
       decoder_1_out11, decoder_1_out12, decoder_1_out13, decoder_1_out14, decoder_1_out15;
  wire [7:0] register_1_q, register_2_q, register_3_q, register_4_q, register_5_q, register_6_q,
       register_7_q, register_8_q, register_9_q, register_10_q, register_11_q, register_12_q, register_13_q,
       register_14_q, register_15_q, register_16_q;

  Clock CLK (.out(CLK_out));
  Decoder #(.select(4)) decoder_1 (
    .out0(decoder_1_out0), .out1(decoder_1_out1), .out2(decoder_1_out2), .out3(decoder_1_out3),
    .out4(decoder_1_out4), .out5(decoder_1_out5), .out6(decoder_1_out6), .out7(decoder_1_out7),
    .out8(decoder_1_out8), .out9(decoder_1_out9), .out10(decoder_1_out10), .out11(decoder_1_out11),
    .out12(decoder_1_out12), .out13(decoder_1_out13), .out14(decoder_1_out14), .out15(decoder_1_out15),
    .sel({in_1, in_2, in_3, in_4}), .en(WRITE_EN));
  Register register_1 (
    .D({in_5, in_6, in_7, in_8, in_9, in_10, in_11, in_12}), .en(decoder_1_out0), .clk(CLK_out),
    .Q(register_1_q));  // open: clr
  Register register_2 (
    .D({in_5, in_6, in_7, in_8, in_9, in_10, in_11, in_12}), .en(decoder_1_out4), .clk(CLK_out),
    .Q(register_2_q));  // open: clr
  Register register_3 (
    .D({in_5, in_6, in_7, in_8, in_9, in_10, in_11, in_12}), .en(decoder_1_out8), .clk(CLK_out),
    .Q(register_3_q));  // open: clr
  Register register_4 (
    .D({in_5, in_6, in_7, in_8, in_9, in_10, in_11, in_12}), .en(decoder_1_out12), .clk(CLK_out),
    .Q(register_4_q));  // open: clr
  Register register_5 (
    .D({in_5, in_6, in_7, in_8, in_9, in_10, in_11, in_12}), .en(decoder_1_out1), .clk(CLK_out),
    .Q(register_5_q));  // open: clr
  Register register_6 (
    .D({in_5, in_6, in_7, in_8, in_9, in_10, in_11, in_12}), .en(decoder_1_out5), .clk(CLK_out),
    .Q(register_6_q));  // open: clr
  Register register_7 (
    .D({in_5, in_6, in_7, in_8, in_9, in_10, in_11, in_12}), .en(decoder_1_out9), .clk(CLK_out),
    .Q(register_7_q));  // open: clr
  Register register_8 (
    .D({in_5, in_6, in_7, in_8, in_9, in_10, in_11, in_12}), .en(decoder_1_out13), .clk(CLK_out),
    .Q(register_8_q));  // open: clr
  Register register_9 (
    .D({in_5, in_6, in_7, in_8, in_9, in_10, in_11, in_12}), .en(decoder_1_out2), .clk(CLK_out),
    .Q(register_9_q));  // open: clr
  Register register_10 (
    .D({in_5, in_6, in_7, in_8, in_9, in_10, in_11, in_12}), .en(decoder_1_out6), .clk(CLK_out),
    .Q(register_10_q));  // open: clr
  Register register_11 (
    .D({in_5, in_6, in_7, in_8, in_9, in_10, in_11, in_12}), .en(decoder_1_out10), .clk(CLK_out),
    .Q(register_11_q));  // open: clr
  Register register_12 (
    .D({in_5, in_6, in_7, in_8, in_9, in_10, in_11, in_12}), .en(decoder_1_out14), .clk(CLK_out),
    .Q(register_12_q));  // open: clr
  Register register_13 (
    .D({in_5, in_6, in_7, in_8, in_9, in_10, in_11, in_12}), .en(decoder_1_out3), .clk(CLK_out),
    .Q(register_13_q));  // open: clr
  Register register_14 (
    .D({in_5, in_6, in_7, in_8, in_9, in_10, in_11, in_12}), .en(decoder_1_out7), .clk(CLK_out),
    .Q(register_14_q));  // open: clr
  Register register_15 (
    .D({in_5, in_6, in_7, in_8, in_9, in_10, in_11, in_12}), .en(decoder_1_out11), .clk(CLK_out),
    .Q(register_15_q));  // open: clr
  Register register_16 (
    .D({in_5, in_6, in_7, in_8, in_9, in_10, in_11, in_12}), .en(decoder_1_out15), .clk(CLK_out),
    .Q(register_16_q));  // open: clr
  Multiplexer #(.enable("true"), .select(4), .width(8)) multiplexer_1 (
    .in0(register_1_q), .in1(register_5_q), .in2(register_9_q), .in3(register_13_q), .in4(register_2_q),
    .in5(register_6_q), .in6(register_10_q), .in7(register_14_q), .in8(register_3_q), .in9(register_7_q),
    .in10(register_11_q), .in11(register_15_q), .in12(register_4_q), .in13(register_8_q),
    .in14(register_12_q), .in15(register_16_q),
    .out({out_19, out_20, out_21, out_22, out_23, out_24, out_25, out_26}),
    .sel({in_15, in_16, in_17, in_18}), .en(READ_EN));

  // Notes on the sheet:
  //   ADDRESS INPUT
  //   DATA INPUT
  //   DATA OUTPUT
  //   8-bit data
  //   16×8-bit RAM module
  //   16 addressable memory locations
  //   128 bits (16 bytes).
  //   ADDRESS INPUT
endmodule
