// Logisim project 16x8_RAM_v2.circ as structural Verilog: 1 circuit, main circuit main
module main (
  input  [3:0] ADDRESS_INPUT,
  input  [7:0] in_2,
  input  [3:0] in_3,
  input  WRITE_EN,
  input  READ_EN,
  output [7:0] out_6
);

  wire clock_1_out, undriven, undriven_2, undriven_3, undriven_4, undriven_5, undriven_6;
  wire [3:0] decoder_1_out0, decoder_1_out4, decoder_1_out8, decoder_1_out12;
  wire [7:0] register_1_q, register_2_q, register_3_q, register_4_q, register_5_q, register_6_q,
       register_7_q, register_8_q, register_9_q, register_10_q, register_11_q, register_12_q, register_16_q;
  wire [31:24] register_13_q, register_14_q, register_15_q;

  Decoder #(.select(4)) decoder_1 (
    .out0(decoder_1_out0[0]), .out1(decoder_1_out0[1]), .out2(decoder_1_out0[2]), .out3(decoder_1_out0[3]),
    .out4(decoder_1_out4[0]), .out5(decoder_1_out4[1]), .out6(decoder_1_out4[2]), .out7(decoder_1_out4[3]),
    .out8(decoder_1_out8[0]), .out9(decoder_1_out8[1]), .out10(decoder_1_out8[2]), .out11(decoder_1_out8[3]),
    .out12(decoder_1_out12[0]), .out13(decoder_1_out12[1]), .out14(decoder_1_out12[2]),
    .out15(decoder_1_out12[3]), .sel(ADDRESS_INPUT), .en(WRITE_EN));
  Clock clock_1 (.out(clock_1_out));
  Register register_1 (.D(in_2), .en(decoder_1_out0[0]), .clk(clock_1_out), .Q(register_1_q));  // open: clr
  Register register_2 (.D(in_2), .en(decoder_1_out4[0]), .clk(undriven), .Q(register_2_q));  // open: clr
  Register register_3 (.D(in_2), .en(decoder_1_out8[0]), .clk(undriven_2), .Q(register_3_q));  // open: clr
  Register register_4 (.D(in_2), .en(decoder_1_out12[0]), .clk(clock_1_out), .Q(register_4_q));  // open: clr
  Register register_5 (.D(in_2), .en(decoder_1_out0[1]), .clk(clock_1_out), .Q(register_5_q), .clr(undriven_3));
  Register register_6 (.D(in_2), .en(decoder_1_out4[1]), .clk(undriven), .Q(register_6_q), .clr(undriven_4));
  Register register_7 (.D(in_2), .en(decoder_1_out8[1]), .clk(undriven_2), .Q(register_7_q), .clr(undriven_5));
  Register register_8 (.D(in_2), .en(decoder_1_out12[1]), .clk(clock_1_out), .Q(register_8_q), .clr(undriven_6));
  Register register_9 (.D(in_2), .en(decoder_1_out0[2]), .clk(clock_1_out), .Q(register_9_q));  // open: clr
  Register register_10 (.D(in_2), .en(decoder_1_out4[2]), .clk(undriven), .Q(register_10_q));  // open: clr
  Register register_11 (.D(in_2), .en(decoder_1_out8[2]), .clk(undriven_2), .Q(register_11_q));  // open: clr
  Register register_12 (.D(in_2), .en(decoder_1_out12[2]), .clk(clock_1_out), .Q(register_12_q));  // open: clr
  Register register_13 (.D(in_2), .en(decoder_1_out0[3]), .clk(clock_1_out), .Q(register_13_q));  // open: clr
  Register register_14 (.D(in_2), .en(decoder_1_out4[3]), .clk(undriven), .Q(register_14_q));  // open: clr
  Register register_15 (.D(in_2), .en(decoder_1_out8[3]), .clk(undriven_2), .Q(register_15_q));  // open: clr
  Register register_16 (.D(in_2), .en(decoder_1_out12[3]), .clk(clock_1_out), .Q(register_16_q));  // open: clr
  Multiplexer #(.enable("true"), .select(4), .width(8)) multiplexer_1 (
    .in0(register_1_q), .in1(register_5_q), .in2(register_9_q), .in3(register_13_q), .in4(register_2_q),
    .in5(register_6_q), .in6(register_10_q), .in7(register_14_q), .in8(register_3_q), .in9(register_7_q),
    .in10(register_11_q), .in11(register_15_q), .in12(register_4_q), .in13(register_8_q),
    .in14(register_12_q), .in15(register_16_q), .out(out_6), .sel(in_3), .en(READ_EN));

  // Notes on the sheet:
  //   8-bit data
  //   16×8-bit RAM module
  //   16 addressable memory locations
  //   128 bits (16 bytes).
  //   DATA INPUT
  //   DATA OUTPUT
  //   ADDRESS INPUT
endmodule
