// Logisim project PROGRAM_COUNTER.circ as structural Verilog: 1 circuit, main circuit main
module main (
  input  A3,
  input  A2,
  input  A1,
  input  A0,
  input  LOAD
);

  wire CLK_out, multiplexer_1_out, multiplexer_2_out, multiplexer_3_out, multiplexer_4_out;
  wire [3:0] adder_1_out, d_ff_4_q;

  Multiplexer multiplexer_1 (.in0(adder_1_out[3]), .in1(A3), .out(multiplexer_1_out), .sel(LOAD));
  Clock CLK (.out(CLK_out));
  D_Flip_Flop d_ff_1 (.D(multiplexer_1_out), .clk(CLK_out), .Q(d_ff_4_q[3]));  // open: Qn, preset, reset
  D_Flip_Flop d_ff_2 (.D(multiplexer_2_out), .clk(CLK_out), .Q(d_ff_4_q[2]));  // open: Qn, preset, reset
  Multiplexer multiplexer_2 (.in0(adder_1_out[2]), .in1(A2), .out(multiplexer_2_out), .sel(LOAD));
  Adder #(.width(4)) adder_1 (.a(4'b0001), .b(d_ff_4_q), .out(adder_1_out));  // open: cin, cout
  D_Flip_Flop d_ff_3 (.D(multiplexer_3_out), .clk(CLK_out), .Q(d_ff_4_q[1]));  // open: Qn, preset, reset
  Multiplexer multiplexer_3 (.in0(adder_1_out[1]), .in1(A1), .out(multiplexer_3_out), .sel(LOAD));
  Multiplexer multiplexer_4 (.in0(adder_1_out[0]), .in1(A0), .out(multiplexer_4_out), .sel(LOAD));
  D_Flip_Flop d_ff_4 (.D(multiplexer_4_out), .clk(CLK_out), .Q(d_ff_4_q[0]));  // open: Qn, preset, reset
endmodule
