// Logisim project 4bit_register.circ as structural Verilog: 1 circuit, main circuit main
module main (
  input  A3,
  input  A2,
  input  A1,
  input  A0,
  input  OP_EN,
  input  LOAD,
  output F3,
  output F2,
  output F1,
  output F0
);

  wire CLK_out, d_ff_1_q, d_ff_2_q, d_ff_3_q, d_ff_4_q, multiplexer_1_out, multiplexer_2_out,
       multiplexer_3_out, multiplexer_4_out;

  Clock CLK (.out(CLK_out));
  D_Flip_Flop d_ff_1 (.D(multiplexer_1_out), .clk(CLK_out), .Q(d_ff_1_q));  // open: Qn, preset, reset
  Multiplexer multiplexer_1 (.in0(d_ff_1_q), .in1(A3), .out(multiplexer_1_out), .sel(LOAD));
  Multiplexer multiplexer_2 (.in0(d_ff_2_q), .in1(A2), .out(multiplexer_2_out), .sel(LOAD));
  assign F3 = OP_EN ? d_ff_1_q : 1'bz;  // Controlled_Buffer F3B
  D_Flip_Flop d_ff_2 (.D(multiplexer_2_out), .clk(CLK_out), .Q(d_ff_2_q));  // open: Qn, preset, reset
  assign F2 = OP_EN ? d_ff_2_q : 1'bz;  // Controlled_Buffer F2B
  assign F1 = OP_EN ? d_ff_3_q : 1'bz;  // Controlled_Buffer F1B
  D_Flip_Flop d_ff_3 (.D(multiplexer_3_out), .clk(CLK_out), .Q(d_ff_3_q));  // open: Qn, preset, reset
  Multiplexer multiplexer_3 (.in0(d_ff_3_q), .in1(A1), .out(multiplexer_3_out), .sel(LOAD));
  assign F0 = OP_EN ? d_ff_4_q : 1'bz;  // Controlled_Buffer F0B
  D_Flip_Flop d_ff_4 (.D(multiplexer_4_out), .clk(CLK_out), .Q(d_ff_4_q));  // open: Qn, preset, reset
  Multiplexer multiplexer_4 (.in0(d_ff_4_q), .in1(A0), .out(multiplexer_4_out), .sel(LOAD));
endmodule
