// Logisim project REGISTER_FILE.circ as structural Verilog: 1 circuit, main circuit main
module main (
  input  READ_EN,
  input  [1:0] READ_REG,
  input  in_3,
  input  in_4,
  input  in_5,
  input  Input,
  input  WRITE_EN,
  input  [1:0] WRITE_REG,
  output out_9,
  output out_10,
  output Output,
  output out_12
);

  wire CLK_out, d_ff_1_q, d_ff_2_q, d_ff_3_q, d_ff_4_q, d_ff_5_q, d_ff_6_q, d_ff_7_q, d_ff_8_q, d_ff_9_q,
       d_ff_10_q, d_ff_11_q, d_ff_12_q, d_ff_13_q, d_ff_14_q, d_ff_15_q, d_ff_16_q, decoder_1_out0,
       decoder_1_out1, decoder_1_out2, decoder_1_out3, decoder_2_out0, decoder_2_out1, decoder_2_out2,
       decoder_2_out3, multiplexer_1_out, multiplexer_2_out, multiplexer_3_out, multiplexer_4_out,
       multiplexer_5_out, multiplexer_6_out, multiplexer_7_out, multiplexer_8_out, multiplexer_9_out,
       multiplexer_10_out, multiplexer_11_out, multiplexer_12_out, multiplexer_13_out, multiplexer_14_out,
       multiplexer_15_out, multiplexer_16_out;

  Clock CLK (.out(CLK_out));
  D_Flip_Flop d_ff_1 (.D(multiplexer_1_out), .clk(CLK_out), .Q(d_ff_1_q));  // open: Qn, preset, reset
  Multiplexer multiplexer_1 (.in0(d_ff_1_q), .in1(in_3), .out(multiplexer_1_out), .sel(decoder_2_out0));
  D_Flip_Flop d_ff_2 (.D(multiplexer_2_out), .clk(CLK_out), .Q(d_ff_2_q));  // open: Qn, preset, reset
  Multiplexer multiplexer_2 (.in0(d_ff_2_q), .in1(in_3), .out(multiplexer_2_out), .sel(decoder_2_out1));
  D_Flip_Flop d_ff_3 (.D(multiplexer_3_out), .clk(CLK_out), .Q(d_ff_3_q));  // open: Qn, preset, reset
  Multiplexer multiplexer_3 (.in0(d_ff_3_q), .in1(in_3), .out(multiplexer_3_out), .sel(decoder_2_out2));
  D_Flip_Flop d_ff_4 (.D(multiplexer_4_out), .clk(CLK_out), .Q(d_ff_4_q));  // open: Qn, preset, reset
  Multiplexer multiplexer_4 (.in0(d_ff_4_q), .in1(in_3), .out(multiplexer_4_out), .sel(decoder_2_out3));
  D_Flip_Flop d_ff_5 (.D(multiplexer_5_out), .clk(CLK_out), .Q(d_ff_5_q));  // open: Qn, preset, reset
  Multiplexer multiplexer_5 (.in0(d_ff_5_q), .in1(in_4), .out(multiplexer_5_out), .sel(decoder_2_out0));
  D_Flip_Flop d_ff_6 (.D(multiplexer_6_out), .clk(CLK_out), .Q(d_ff_6_q));  // open: Qn, preset, reset
  Multiplexer multiplexer_6 (.in0(d_ff_6_q), .in1(in_4), .out(multiplexer_6_out), .sel(decoder_2_out1));
  D_Flip_Flop d_ff_7 (.D(multiplexer_7_out), .clk(CLK_out), .Q(d_ff_7_q));  // open: Qn, preset, reset
  Multiplexer multiplexer_7 (.in0(d_ff_7_q), .in1(in_4), .out(multiplexer_7_out), .sel(decoder_2_out2));
  D_Flip_Flop d_ff_8 (.D(multiplexer_8_out), .clk(CLK_out), .Q(d_ff_8_q));  // open: Qn, preset, reset
  Multiplexer multiplexer_8 (.in0(d_ff_8_q), .in1(in_4), .out(multiplexer_8_out), .sel(decoder_2_out3));
  assign out_9 = decoder_1_out0 ? d_ff_1_q : 1'bz;  // Controlled_Buffer controlled_buffer_1
  assign out_10 = decoder_1_out0 ? d_ff_5_q : 1'bz;  // Controlled_Buffer controlled_buffer_2
  assign out_9 = decoder_1_out1 ? d_ff_2_q : 1'bz;  // Controlled_Buffer controlled_buffer_3
  assign out_10 = decoder_1_out1 ? d_ff_6_q : 1'bz;  // Controlled_Buffer controlled_buffer_4
  assign out_9 = decoder_1_out2 ? d_ff_3_q : 1'bz;  // Controlled_Buffer controlled_buffer_5
  assign out_10 = decoder_1_out2 ? d_ff_7_q : 1'bz;  // Controlled_Buffer controlled_buffer_6
  assign out_9 = decoder_1_out3 ? d_ff_4_q : 1'bz;  // Controlled_Buffer controlled_buffer_7
  assign out_10 = decoder_1_out3 ? d_ff_8_q : 1'bz;  // Controlled_Buffer controlled_buffer_8
  assign Output = decoder_1_out0 ? d_ff_9_q : 1'bz;  // Controlled_Buffer controlled_buffer_9
  assign out_12 = decoder_1_out0 ? d_ff_13_q : 1'bz;  // Controlled_Buffer controlled_buffer_10
  D_Flip_Flop d_ff_9 (.D(multiplexer_9_out), .clk(CLK_out), .Q(d_ff_9_q));  // open: Qn, preset, reset
  Multiplexer multiplexer_9 (.in0(d_ff_9_q), .in1(in_5), .out(multiplexer_9_out), .sel(decoder_2_out0));
  assign Output = decoder_1_out1 ? d_ff_10_q : 1'bz;  // Controlled_Buffer controlled_buffer_11
  assign out_12 = decoder_1_out1 ? d_ff_14_q : 1'bz;  // Controlled_Buffer controlled_buffer_12
  D_Flip_Flop d_ff_10 (.D(multiplexer_10_out), .clk(CLK_out), .Q(d_ff_10_q));  // open: Qn, preset, reset
  Multiplexer multiplexer_10 (.in0(d_ff_10_q), .in1(in_5), .out(multiplexer_10_out), .sel(decoder_2_out1));
  assign Output = decoder_1_out2 ? d_ff_11_q : 1'bz;  // Controlled_Buffer controlled_buffer_13
  assign out_12 = decoder_1_out2 ? d_ff_15_q : 1'bz;  // Controlled_Buffer controlled_buffer_14
  D_Flip_Flop d_ff_11 (.D(multiplexer_11_out), .clk(CLK_out), .Q(d_ff_11_q));  // open: Qn, preset, reset
  Multiplexer multiplexer_11 (.in0(d_ff_11_q), .in1(in_5), .out(multiplexer_11_out), .sel(decoder_2_out2));
  assign Output = decoder_1_out3 ? d_ff_12_q : 1'bz;  // Controlled_Buffer controlled_buffer_15
  assign out_12 = decoder_1_out3 ? d_ff_16_q : 1'bz;  // Controlled_Buffer controlled_buffer_16
  D_Flip_Flop d_ff_12 (.D(multiplexer_12_out), .clk(CLK_out), .Q(d_ff_12_q));  // open: Qn, preset, reset
  Multiplexer multiplexer_12 (.in0(d_ff_12_q), .in1(in_5), .out(multiplexer_12_out), .sel(decoder_2_out3));
  D_Flip_Flop d_ff_13 (.D(multiplexer_13_out), .clk(CLK_out), .Q(d_ff_13_q));  // open: Qn, preset, reset
  Multiplexer multiplexer_13 (.in0(d_ff_13_q), .in1(Input), .out(multiplexer_13_out), .sel(decoder_2_out0));
  D_Flip_Flop d_ff_14 (.D(multiplexer_14_out), .clk(CLK_out), .Q(d_ff_14_q));  // open: Qn, preset, reset
  Multiplexer multiplexer_14 (.in0(d_ff_14_q), .in1(Input), .out(multiplexer_14_out), .sel(decoder_2_out1));
  D_Flip_Flop d_ff_15 (.D(multiplexer_15_out), .clk(CLK_out), .Q(d_ff_15_q));  // open: Qn, preset, reset
  Multiplexer multiplexer_15 (.in0(d_ff_15_q), .in1(Input), .out(multiplexer_15_out), .sel(decoder_2_out2));
  D_Flip_Flop d_ff_16 (.D(multiplexer_16_out), .clk(CLK_out), .Q(d_ff_16_q));  // open: Qn, preset, reset
  Multiplexer multiplexer_16 (.in0(d_ff_16_q), .in1(Input), .out(multiplexer_16_out), .sel(decoder_2_out3));
  Decoder #(.select(2)) decoder_1 (
    .out0(decoder_1_out0), .out1(decoder_1_out1), .out2(decoder_1_out2), .out3(decoder_1_out3),
    .sel(READ_REG), .en(READ_EN));
  Decoder #(.select(2)) decoder_2 (
    .out0(decoder_2_out0), .out1(decoder_2_out1), .out2(decoder_2_out2), .out3(decoder_2_out3),
    .sel(WRITE_REG), .en(WRITE_EN));

  // Notes on the sheet:
  //   R0
  //   R1
  //   R2
  //   R3
  //   Input bus
  //   Output bus
  //   4-bit Register File
  //   4 Registers
  //   1 Read Port
  //   1 Write Port
  //   Shared Bus Architecture
endmodule
