// Logisim project register_file_v2.circ as structural Verilog: 1 circuit, main circuit main
module main (
  input  [3:0] in_1,
  input  write_en,
  input  [1:0] in_3,
  input  [1:0] in_4,
  input  read_en,
  output [3:0] out_6
);

  wire clock_1_out, decoder_1_out0, decoder_1_out1, decoder_1_out2, decoder_1_out3, decoder_2_out0,
       decoder_2_out1, decoder_2_out2, decoder_2_out3, multiplexer_1_out, multiplexer_2_out,
       multiplexer_3_out, multiplexer_4_out, multiplexer_5_out, multiplexer_6_out, multiplexer_7_out,
       multiplexer_8_out, multiplexer_9_out, multiplexer_10_out, multiplexer_11_out, multiplexer_12_out,
       multiplexer_13_out, multiplexer_14_out, multiplexer_15_out, multiplexer_16_out;
  wire [3:0] d_ff_13_q, d_ff_14_q, d_ff_15_q, d_ff_16_q;

  Multiplexer multiplexer_1 (.in0(d_ff_13_q[3]), .in1(in_1[3]), .out(multiplexer_1_out), .sel(decoder_1_out0));
  Multiplexer multiplexer_2 (.in0(d_ff_14_q[3]), .in1(in_1[3]), .out(multiplexer_2_out), .sel(decoder_1_out1));
  Multiplexer multiplexer_3 (.in0(d_ff_15_q[3]), .in1(in_1[3]), .out(multiplexer_3_out), .sel(decoder_1_out2));
  Multiplexer multiplexer_4 (.in0(d_ff_16_q[3]), .in1(in_1[3]), .out(multiplexer_4_out), .sel(decoder_1_out3));
  D_Flip_Flop d_ff_1 (.D(multiplexer_1_out), .clk(clock_1_out), .Q(d_ff_13_q[3]));  // open: Qn, preset, reset
  D_Flip_Flop d_ff_2 (.D(multiplexer_2_out), .clk(clock_1_out), .Q(d_ff_14_q[3]));  // open: Qn, preset, reset
  D_Flip_Flop d_ff_3 (.D(multiplexer_3_out), .clk(clock_1_out), .Q(d_ff_15_q[3]));  // open: Qn, preset, reset
  D_Flip_Flop d_ff_4 (.D(multiplexer_4_out), .clk(clock_1_out), .Q(d_ff_16_q[3]));  // open: Qn, preset, reset
  D_Flip_Flop d_ff_5 (.D(multiplexer_5_out), .clk(clock_1_out), .Q(d_ff_13_q[2]));  // open: Qn, preset, reset
  Multiplexer multiplexer_5 (.in0(d_ff_13_q[2]), .in1(in_1[2]), .out(multiplexer_5_out), .sel(decoder_1_out0));
  D_Flip_Flop d_ff_6 (.D(multiplexer_6_out), .clk(clock_1_out), .Q(d_ff_14_q[2]));  // open: Qn, preset, reset
  Multiplexer multiplexer_6 (.in0(d_ff_14_q[2]), .in1(in_1[2]), .out(multiplexer_6_out), .sel(decoder_1_out1));
  D_Flip_Flop d_ff_7 (.D(multiplexer_7_out), .clk(clock_1_out), .Q(d_ff_15_q[2]));  // open: Qn, preset, reset
  Multiplexer multiplexer_7 (.in0(d_ff_15_q[2]), .in1(in_1[2]), .out(multiplexer_7_out), .sel(decoder_1_out2));
  D_Flip_Flop d_ff_8 (.D(multiplexer_8_out), .clk(clock_1_out), .Q(d_ff_16_q[2]));  // open: Qn, preset, reset
  Multiplexer multiplexer_8 (.in0(d_ff_16_q[2]), .in1(in_1[2]), .out(multiplexer_8_out), .sel(decoder_1_out3));
  D_Flip_Flop d_ff_9 (.D(multiplexer_9_out), .clk(clock_1_out), .Q(d_ff_13_q[1]));  // open: Qn, preset, reset
  Multiplexer multiplexer_9 (.in0(d_ff_13_q[1]), .in1(in_1[1]), .out(multiplexer_9_out), .sel(decoder_1_out0));
  D_Flip_Flop d_ff_10 (.D(multiplexer_10_out), .clk(clock_1_out), .Q(d_ff_14_q[1]));  // open: Qn, preset, reset
  Multiplexer multiplexer_10 (.in0(d_ff_14_q[1]), .in1(in_1[1]), .out(multiplexer_10_out), .sel(decoder_1_out1));
  D_Flip_Flop d_ff_11 (.D(multiplexer_11_out), .clk(clock_1_out), .Q(d_ff_15_q[1]));  // open: Qn, preset, reset
  Multiplexer multiplexer_11 (.in0(d_ff_15_q[1]), .in1(in_1[1]), .out(multiplexer_11_out), .sel(decoder_1_out2));
  D_Flip_Flop d_ff_12 (.D(multiplexer_12_out), .clk(clock_1_out), .Q(d_ff_16_q[1]));  // open: Qn, preset, reset
  Multiplexer multiplexer_12 (.in0(d_ff_16_q[1]), .in1(in_1[1]), .out(multiplexer_12_out), .sel(decoder_1_out3));
  assign out_6 = decoder_2_out0 ? d_ff_13_q : 4'bz;  // Controlled_Buffer controlled_buffer_1
  D_Flip_Flop d_ff_13 (.D(multiplexer_13_out), .clk(clock_1_out), .Q(d_ff_13_q[0]));  // open: Qn, preset, reset
  Multiplexer multiplexer_13 (.in0(d_ff_13_q[0]), .in1(in_1[0]), .out(multiplexer_13_out), .sel(decoder_1_out0));
  assign out_6 = decoder_2_out1 ? d_ff_14_q : 4'bz;  // Controlled_Buffer controlled_buffer_2
  D_Flip_Flop d_ff_14 (.D(multiplexer_14_out), .clk(clock_1_out), .Q(d_ff_14_q[0]));  // open: Qn, preset, reset
  Multiplexer multiplexer_14 (.in0(d_ff_14_q[0]), .in1(in_1[0]), .out(multiplexer_14_out), .sel(decoder_1_out1));
  assign out_6 = decoder_2_out2 ? d_ff_15_q : 4'bz;  // Controlled_Buffer controlled_buffer_3
  D_Flip_Flop d_ff_15 (.D(multiplexer_15_out), .clk(clock_1_out), .Q(d_ff_15_q[0]));  // open: Qn, preset, reset
  Multiplexer multiplexer_15 (.in0(d_ff_15_q[0]), .in1(in_1[0]), .out(multiplexer_15_out), .sel(decoder_1_out2));
  assign out_6 = decoder_2_out3 ? d_ff_16_q : 4'bz;  // Controlled_Buffer controlled_buffer_4
  D_Flip_Flop d_ff_16 (.D(multiplexer_16_out), .clk(clock_1_out), .Q(d_ff_16_q[0]));  // open: Qn, preset, reset
  Multiplexer multiplexer_16 (.in0(d_ff_16_q[0]), .in1(in_1[0]), .out(multiplexer_16_out), .sel(decoder_1_out3));
  Decoder #(.select(2)) decoder_1 (
    .out0(decoder_1_out0), .out1(decoder_1_out1), .out2(decoder_1_out2), .out3(decoder_1_out3), .sel(in_3),
    .en(write_en));
  Decoder #(.select(2)) decoder_2 (
    .out0(decoder_2_out0), .out1(decoder_2_out1), .out2(decoder_2_out2), .out3(decoder_2_out3), .sel(in_4),
    .en(read_en));
  Clock clock_1 (.out(clock_1_out));
endmodule
